// Logisim project Abacus_2_New.circ as structural Verilog
module northbridge (
  input  [7:0] B,
  input  [15:0] A
);

  wire BANKMAN, mmu_1_ram, mmu_1_rom, SOUTHBRIDGE;

  mmu mmu_1 (.B(B), .A(A), .BANK(BANKMAN), .ROM(mmu_1_rom), .RAM(mmu_1_ram), .IO(SOUTHBRIDGE));
endmodule

module mmu (
  input  [7:0] B,
  input  [15:0] A,
  output BANK,
  output ROM,
  output RAM,
  output IO
);

  wire and_1_out, and_2_out, and_3_out, and_5_out, and_6_out, and_7_out, nor_1_out, nor_2_out, not_1_out,
       not_2_out;

  not not_1 (not_1_out, B[6]);
  and and_1 (and_1_out, A[14], A[15]);
  not not_2 (not_2_out, A[13]);
  and and_2 (and_2_out, B[6], B[7]);
  and and_3 (and_3_out, not_1_out, B[7]);
  and and_4 (BANK, and_1_out, not_2_out);
  and and_5 (and_5_out, and_1_out, A[13]);
  and and_6 (and_6_out, B[5], and_3_out);
  or or_1 (ROM, and_5_out, and_7_out);
  and and_7 (and_7_out, BANK, and_6_out);
  or or_2 (RAM, nor_2_out, nor_1_out);
  nor nor_1 (nor_1_out, BANK, and_5_out);
  and and_8 (IO, BANK, and_2_out);
  nor nor_2 (nor_2_out, and_7_out, IO);
endmodule

module mmu_nano (
  input  [15:0] A,
  output ROM,
  output IO,
  output RAM
);

  wire and_1_out, nor_1_out;

  nor nor_1 (nor_1_out, A[13], A[13]);
  and and_1 (and_1_out, A[14], A[15]);
  and and_2 (IO, nor_1_out, and_1_out);
  and and_3 (ROM, and_1_out, A[13]);
  nor nor_2 (RAM, IO, ROM);
endmodule

module waitstategen (
  input  iM1,
  input  iCLK,
  output iWAIT
);

  wire d_ff_2_q, not_1_out;

  not not_1 (not_1_out, d_ff_2_q);
  D_Flip_Flop d_ff_1 (.D(iM1), .clk(iCLK), .Q(iWAIT), .preset(not_1_out), .reset(1'b0));  // open: Qn
  D_Flip_Flop d_ff_2 (.D(iWAIT), .clk(iCLK), .Q(d_ff_2_q), .preset(1'b0), .reset(1'b0));  // open: Qn
endmodule
